# Fritzing sketch breadboard (saved by Fritzing 0.9.2b)
breadboards: 1

parts:
  U2 = attiny85 [package=dip]
  U3 = POT [package=pot_mammoth]
  U4 = POT [package=pot_mammoth]
  S2 = Momentary Switch [package=ksa_sealed_tac_switch]
  S3 = Momentary Switch [package=ksa_sealed_tac_switch]
  SPKR1 = Loudspeaker
  IC1 = Voltage Regulator [package=to-220-alt]
  VCC1 = Battery block 9V

nets:
  N1: U2.Pin_2, S2.3
  N2: U2.Pin_3, U3.A
  N3: U2.Pin_4, U3.E, U4.E, S2.1, S3.1, SPKR1.pin1, IC1.GND, VCC1.-
  N4: U2.Pin_5, SPKR1.pin2
  N5: U2.Pin_6, S3.3
  N6: U2.Pin_7, U4.A
  N7: U2.Pin_8, U3.S, U4.S, IC1.OUT
  N8: IC1.IN, VCC1.+
