# Fritzing sketch breadboard (saved by Fritzing 0.9.2b)
breadboards: 1

parts:
  U2 = attiny85 [package=dip]
  7805 = Voltage Regulator [package=to-220-alt]
  VCC1 = Battery block 9V
  SPKR1 = Loudspeaker

nets:
  N1: U2.Pin_5, SPKR1.pin2
  N2: U2.Pin_8, 7805.OUT
  N3: 7805.GND, VCC1.-, SPKR1.pin1
  N4: 7805.IN, VCC1.+
