# Fritzing sketch breadboard (saved by Fritzing 0.9.2b)
breadboards: 1

parts:
  7805 = Voltage Regulator [package=to-220-alt]
  VCC1 = Battery block 9V
  SPKR1 = Loudspeaker
  Pot1_/_Tempo = POT [package=pot_mammoth]
  Pot2_/_BitCrusher! = POT [package=pot_mammoth]
  U2 = attiny85 [package=dip]

nets:
  N1: 7805.GND, VCC1.-, SPKR1.pin1, Pot1_/_Tempo.S, Pot2_/_BitCrusher!.S
  N2: 7805.IN, VCC1.+
  N3: 7805.OUT, Pot1_/_Tempo.E, Pot2_/_BitCrusher!.E, U2.Pin_8
  N4: SPKR1.pin2, U2.Pin_6
  N5: Pot1_/_Tempo.A, U2.Pin_3
  N6: Pot2_/_BitCrusher!.A, U2.Pin_7
